# Fritzing sketch sketch (saved by Fritzing 0.9.3b)

parts:
  U1 = NodeMCU V3.0
  J1 = Piezo Speaker
  R1 = Resistor [tolerance=±5% resistance=100 package=THT]

nets:
  N1: U1.D1, R1.Pin_1
  N2: U1.GND, J1.pin1
  N3: J1.pin2, R1.Pin_0

custom parts:
  NodeMCU V3.0: ESP8266 based NodeMCU
